# Fritzing sketch 02_light_analog (saved by Fritzing 0.9.3b)
breadboards: 1

parts:
  R1 = Resistor [tolerance=±5% resistance=100k package="1206 [SMD]"]
  WeMos_D1_Mini1 = WeMos D1 Mini
  R2 = Photocell (LDR) [package=THT]

nets:
  N1: R1.Pin_0, WeMos_D1_Mini1.G
  N2: R1.Pin_1, R2.pin_0
  N3: WeMos_D1_Mini1.3V3, R2.pin_1
