# Fritzing sketch 04_rgb_led (saved by Fritzing 0.9.3b)
breadboards: 1

parts:
  WeMos_D1_Mini1 = WeMos D1 Mini
  Часть1 = ws2812b [package="smd 2812b"]

nets:
  3V3: WeMos_D1_Mini1.3V3, Часть1.VDD
  N1: WeMos_D1_Mini1.D7, Часть1.DIN
  N2: WeMos_D1_Mini1.G, Часть1.VSS
